# Fritzing sketch mailbox_ESP32CAM_AI_THINKER_v2 (saved by Fritzing 0.9.4)

parts:
  S3 = SWITCH-MOMENTARY-2 [package=reed_switch_pth]
  S4 = SWITCH-MOMENTARY-2 [package=reed_switch_pth]
  Composant6 = Solar Cell
  BAT1 = 18650 battery holder [package=battery-18650-kit]
  Solar_LiPo_Charger1 = Solar LiPo Charger
  D1 = Schottky Diode [part_number=1N5817 package="300 mil [THT]"]
  ESP32_-_Back1 = ESP32 - CAM
  S6 = Pushbutton [package=THT]
  LED1 = smd LED [color="Red (633nm)" package="0805 [SMD]"]

nets:
  N1: S3.1, S4.1, ESP32_-_Back1.GPIO12
  N2: Composant6.+, D1.anode
  N3: Composant6.-, BAT1.-, Solar_LiPo_Charger1.Solar_In-, Solar_LiPo_Charger1.LiPo-, Solar_LiPo_Charger1.Out-, ESP32_-_Back1.GND#7
  N4: BAT1.+, Solar_LiPo_Charger1.LiPo+
  N5: Solar_LiPo_Charger1.Solar_In+, D1.cathode
  N6: Solar_LiPo_Charger1.Out+, ESP32_-_Back1.5V
  N7: ESP32_-_Back1.GPIO13, LED1.anode
  N8: ESP32_-_Back1.GPIO16, S6.leg0
  N9: ESP32_-_Back1.GND#16, S6.leg1

notes:
  100 Ohms
  Light Contrast
  Motor
  Wake Up Manual
  Mailbox Notifier - ESP32 CAM - AI THINKER
  10 KOhms
  VBatt 5 Volts
  ESP32 CAM - AI THINKER
  vincent.huynen@gmail.com - novembre 2020 - Version 1
  5 Volts
  Reed Swith -  NC : Normally Closed
  Flip Door
  Solar LiPo Power Regulator
  Solar Panel
  GPIO16
  Internal PULL-UP
  GND
  GPIO12
  Blinking LED
  GPIO13

custom parts:
  18650 battery holder: 18650 Battery Holder
  Solar LiPo Charger: The Solar LiPo Charger board is a single cell LiPo boost converter (to 3.3V and 5V), solar and micro-USB charger in one. The board comes with (3) JST connectors for a single cell LiPo battery, a solar panel and an output load, a micro-USB connector for the 5V charge input, and a USB-A connector for 5V load output. The board is a stand-alone item and is not intended to be soldered to a PCB,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
  ESP32 - CAM: The ESP32-CAM has a very competitive small-size camera module that can operate independently as a minimum system with a footprint of only 27*40.5*4.5mm and a deep sleep current of up to 6mA.
